# Fritzing sketch cryptopi_schematics (saved by Fritzing 0.9.6b)
breadboards: 1

parts:
  RE1 = Rotary Encoder [package=THT]  # not connected
  R1 = Resistor [tolerance=±5% power=0.25 resistance=10k package=THT]
  R2 = Resistor [tolerance=±5% power=0.25 resistance=10k package=THT]
  S1 = Pushbutton [package="[THT]"]
  R3 = Resistor [tolerance=±5% power=0.25 resistance=100 package=THT]
  MCU1 = Raspberry Pi Zero
  LCD2004-I2C1 = LCD2004-I2C

nets:
  N1: R1.Pin_0, MCU1.pin_16
  N2: R1.Pin_1, R2.Pin_1, MCU1.pin_17
  N3: R2.Pin_0, MCU1.pin_18
  N4: S1.Pin_1, S1.Pin_2, R3.Pin_1
  N5: S1.Pin_3, S1.Pin_4, MCU1.pin_40
  N6: R3.Pin_0, MCU1.pin_6, MCU1.pin_8, MCU1.pin_34, MCU1.pin_39, LCD2004-I2C1.GND
  N7: MCU1.pin_3, LCD2004-I2C1.SDA
  N8: MCU1.pin_4, LCD2004-I2C1.VCC
  N9: MCU1.pin_5, MCU1.pin_7, LCD2004-I2C1.SCL

custom parts:
  LCD2004-I2C: A standard character display with 4x20 characters. Comes in many colors with LCM2004 IIC attached.
